// Logisim project 4digits.circ as structural Verilog: 1 circuit, main circuit main
module main (
  input  [15:0] Input,
  output [15:0] Output
);

  wire and_1_out, and_2_out, and_3_out, and_4_out, and_5_out, and_6_out, and_7_out, and_8_out, and_9_out,
       and_10_out, and_11_out, and_12_out, and_13_out, not_1_out, not_2_out, not_9_out, not_10_out,
       not_11_out, not_13_out, not_14_out;

  not not_1 (not_1_out, Input[15]);
  not not_2 (not_2_out, Input[14]);
  not not_3 (Output[13], Input[13]);
  Hex_Digit_Display hex_digit_display_1 (.value({Output[15:13], Input[12]}));  // open: dp
  // NOT_Gate not_4 has open pins: in=Input[12], out=open
  Hex_Digit_Display hex_digit_display_2 (.value(Input[15:12]));  // open: dp
  xor xor_1 (Output[14], Input[14], Input[13]);
  and and_1 (and_1_out, Input[15], Output[13]);
  and and_2 (and_2_out, not_1_out, Input[14], Input[13]);
  and and_3 (and_3_out, Input[15], not_2_out);
  or or_1 (Output[15], and_1_out, and_2_out, and_3_out);
  not not_5 (Output[10], Input[10]);
  // NOT_Gate not_6 has open pins: in=Input[11], out=open
  Hex_Digit_Display hex_digit_display_3 (.value({Output[11:10], Input[9:8]}));  // open: dp
  // NOT_Gate not_7 has open pins: in=Input[8], out=open
  // NOT_Gate not_8 has open pins: in=Input[9], out=open
  Hex_Digit_Display hex_digit_display_4 (.value(Input[11:8]));  // open: dp
  xor xor_2 (Output[11], Input[11], Input[10]);
  not not_9 (not_9_out, Input[7]);
  not not_10 (not_10_out, Input[5]);
  not not_11 (not_11_out, Input[6]);
  Hex_Digit_Display hex_digit_display_5 (.value(Output[7:4]));  // open: dp
  Hex_Digit_Display hex_digit_display_6 (.value(Input[7:4]));  // open: dp
  not not_12 (Output[4], Input[4]);
  and and_4 (and_4_out, not_11_out, not_10_out);
  and and_5 (and_5_out, Input[6], Input[5], Input[4]);
  and and_6 (and_6_out, not_11_out, Output[4]);
  and and_7 (and_7_out, not_9_out, Input[6]);
  and and_8 (and_8_out, not_9_out, Input[5], Input[4]);
  and and_9 (and_9_out, Input[7], not_11_out, Output[4]);
  and and_10 (and_10_out, Input[7], not_11_out, not_10_out);
  xor xor_3 (Output[5], Input[5], Input[4]);
  or or_2 (Output[6], and_4_out, and_5_out, and_6_out);
  or or_3 (Output[7], and_7_out, and_8_out, and_9_out, and_10_out);
  not not_13 (not_13_out, Input[3]);
  not not_14 (not_14_out, Input[2]);
  not not_15 (Output[1], Input[1]);
  Hex_Digit_Display hex_digit_display_7 (.value({Output[3:1], Input[0]}));  // open: dp
  // NOT_Gate not_16 has open pins: in=Input[0], out=open
  Hex_Digit_Display hex_digit_display_8 (.value(Input[3:0]));  // open: dp
  xor xor_4 (Output[2], Input[2], Input[1]);
  and and_11 (and_11_out, Input[3], Output[1]);
  and and_12 (and_12_out, not_13_out, Input[2], Input[1]);
  and and_13 (and_13_out, Input[3], not_14_out);
  or or_4 (Output[3], and_11_out, and_12_out, and_13_out);

  assign {Output[12], Output[9:8], Output[0]} = {Input[12], Input[9:8], Input[0]};

  // Notes on the sheet:
  //   Input: pull=down
  //   1er caracter
  //   2o caracter
  //   3er caracter
  //   4o caracter
endmodule
