// Logisim project 8digits.circ as structural Verilog: 1 circuit, main circuit main
module main (
  input  [31:0] Input,
  output [31:0] out_2
);

  wire and_1_out, and_2_out, and_3_out, and_4_out, and_5_out, and_6_out, and_7_out, and_8_out, and_9_out,
       and_10_out, and_11_out, and_12_out, and_13_out, and_14_out, and_15_out, and_16_out, and_17_out,
       and_18_out, and_19_out, and_20_out, and_21_out, and_22_out, and_23_out, not_1_out, not_3_out,
       not_9_out, not_10_out, not_11_out, not_13_out, not_14_out, not_21_out, not_22_out, not_23_out,
       not_25_out, not_27_out;

  not not_1 (not_1_out, Input[31]);
  not not_2 (out_2[29], Input[29]);
  not not_3 (not_3_out, Input[30]);
  Hex_Digit_Display hex_digit_display_1 (.value({out_2[31:29], Input[28]}));  // open: dp
  // NOT_Gate not_4 has open pins: in=Input[28], out=open
  Hex_Digit_Display hex_digit_display_2 (.value(Input[31:28]));  // open: dp
  xor xor_1 (out_2[30], Input[30], Input[29]);
  and and_1 (and_1_out, Input[31], out_2[29]);
  and and_2 (and_2_out, not_1_out, Input[30], Input[29]);
  and and_3 (and_3_out, Input[31], not_3_out);
  or or_1 (out_2[31], and_1_out, and_2_out, and_3_out);
  // NOT_Gate not_5 has open pins: in=Input[27], out=open
  not not_6 (out_2[26], Input[26]);
  Hex_Digit_Display hex_digit_display_3 (.value({out_2[27:26], Input[25:24]}));  // open: dp
  // NOT_Gate not_7 has open pins: in=Input[24], out=open
  // NOT_Gate not_8 has open pins: in=Input[25], out=open
  Hex_Digit_Display hex_digit_display_4 (.value(Input[27:24]));  // open: dp
  xor xor_2 (out_2[27], Input[27], Input[26]);
  not not_9 (not_9_out, Input[23]);
  not not_10 (not_10_out, Input[22]);
  not not_11 (not_11_out, Input[21]);
  Hex_Digit_Display hex_digit_display_5 (.value(out_2[23:20]));  // open: dp
  not not_12 (out_2[20], Input[20]);
  and and_4 (and_4_out, not_10_out, not_11_out);
  and and_5 (and_5_out, Input[22], Input[21], Input[20]);
  and and_6 (and_6_out, not_10_out, out_2[20]);
  and and_7 (and_7_out, not_9_out, Input[22]);
  and and_8 (and_8_out, not_9_out, Input[21], Input[20]);
  and and_9 (and_9_out, Input[23], not_10_out, out_2[20]);
  and and_10 (and_10_out, Input[23], not_10_out, not_11_out);
  Hex_Digit_Display hex_digit_display_6 (.value(Input[23:20]));  // open: dp
  xor xor_3 (out_2[21], Input[21], Input[20]);
  or or_2 (out_2[22], and_4_out, and_5_out, and_6_out);
  or or_3 (out_2[23], and_7_out, and_8_out, and_9_out, and_10_out);
  not not_13 (not_13_out, Input[19]);
  not not_14 (not_14_out, Input[18]);
  not not_15 (out_2[17], Input[17]);
  Hex_Digit_Display hex_digit_display_7 (.value({out_2[19:17], Input[16]}));  // open: dp
  Hex_Digit_Display hex_digit_display_8 (.value(Input[19:16]));  // open: dp
  // NOT_Gate not_16 has open pins: in=Input[16], out=open
  xor xor_4 (out_2[18], Input[18], Input[17]);
  and and_11 (and_11_out, Input[19], out_2[17]);
  and and_12 (and_12_out, not_13_out, Input[18], Input[17]);
  and and_13 (and_13_out, Input[19], not_14_out);
  or or_4 (out_2[19], and_11_out, and_12_out, and_13_out);
  not not_17 (out_2[14], Input[14]);
  // NOT_Gate not_18 has open pins: in=Input[15], out=open
  Hex_Digit_Display hex_digit_display_9 (.value({out_2[15:14], Input[13:12]}));  // open: dp
  // NOT_Gate not_19 has open pins: in=Input[13], out=open
  // NOT_Gate not_20 has open pins: in=Input[12], out=open
  Hex_Digit_Display hex_digit_display_10 (.value(Input[15:12]));  // open: dp
  xor xor_5 (out_2[15], Input[15], Input[14]);
  not not_21 (not_21_out, Input[11]);
  not not_22 (not_22_out, Input[9]);
  not not_23 (not_23_out, Input[10]);
  Hex_Digit_Display hex_digit_display_11 (.value(out_2[11:8]));  // open: dp
  Hex_Digit_Display hex_digit_display_12 (.value(Input[11:8]));  // open: dp
  not not_24 (out_2[8], Input[8]);
  and and_14 (and_14_out, not_23_out, not_22_out);
  and and_15 (and_15_out, Input[10], Input[9], Input[8]);
  and and_16 (and_16_out, not_23_out, out_2[8]);
  and and_17 (and_17_out, not_21_out, Input[10]);
  and and_18 (and_18_out, not_21_out, Input[9], Input[8]);
  and and_19 (and_19_out, Input[11], not_23_out, out_2[8]);
  and and_20 (and_20_out, Input[11], not_23_out, not_22_out);
  xor xor_6 (out_2[9], Input[9], Input[8]);
  or or_5 (out_2[10], and_14_out, and_15_out, and_16_out);
  or or_6 (out_2[11], and_17_out, and_18_out, and_19_out, and_20_out);
  not not_25 (not_25_out, Input[7]);
  not not_26 (out_2[5], Input[5]);
  not not_27 (not_27_out, Input[6]);
  Hex_Digit_Display hex_digit_display_13 (.value({out_2[7:5], Input[4]}));  // open: dp
  // NOT_Gate not_28 has open pins: in=Input[4], out=open
  Hex_Digit_Display hex_digit_display_14 (.value(Input[7:4]));  // open: dp
  xor xor_7 (out_2[6], Input[6], Input[5]);
  and and_21 (and_21_out, Input[7], out_2[5]);
  and and_22 (and_22_out, not_25_out, Input[6], Input[5]);
  and and_23 (and_23_out, Input[7], not_27_out);
  or or_7 (out_2[7], and_21_out, and_22_out, and_23_out);
  // NOT_Gate not_29 has open pins: in=Input[3], out=open
  not not_30 (out_2[2], Input[2]);
  Hex_Digit_Display hex_digit_display_15 (.value({out_2[3:2], Input[1:0]}));  // open: dp
  // NOT_Gate not_31 has open pins: in=Input[0], out=open
  // NOT_Gate not_32 has open pins: in=Input[1], out=open
  Hex_Digit_Display hex_digit_display_16 (.value(Input[3:0]));  // open: dp
  xor xor_8 (out_2[3], Input[3], Input[2]);

  assign {out_2[28], out_2[25:24], out_2[16], out_2[13:12], out_2[4], out_2[1:0]} = {Input[28], Input[25:24], Input[16], Input[13:12], Input[4], Input[1:0]};

  // Notes on the sheet:
  //   Input: pull=down
  //   1er caracter
  //   2o caracter
  //   3er caracter
  //   4o caracter
  //   5o caracter
  //   6o caracter
  //   7o caracter
  //   8o caracter
endmodule
