// Logisim project base3.circ as structural Verilog: 1 circuit, main circuit main
module main (
  input  [3:0] in_1,
  input  [3:0] in_2,
  input  [3:0] in_3,
  input  [3:0] in_4
);

  wire and_1_out, and_2_out, and_3_out, and_4_out, and_5_out, and_6_out, and_7_out, and_8_out, and_9_out,
       and_10_out, and_11_out, and_12_out, and_13_out, not_1_out, not_3_out, not_9_out, not_10_out,
       not_11_out, not_13_out, not_14_out;
  wire [3:0] not_12_out;
  wire [3:1] not_2_out, not_15_out;
  wire [3:2] not_5_out;

  not not_1 (not_1_out, in_1[3]);
  not not_2 (not_2_out[1], in_1[1]);
  not not_3 (not_3_out, in_1[2]);
  Hex_Digit_Display hex_digit_display_1 (.value({not_2_out, in_1[0]}));  // open: dp
  // NOT_Gate not_4 has open pins: in=in_1[0], out=open
  xor xor_1 (not_2_out[2], in_1[2], in_1[1]);
  and and_1 (and_1_out, in_1[3], not_2_out[1]);
  and and_2 (and_2_out, not_1_out, in_1[2], in_1[1]);
  and and_3 (and_3_out, in_1[3], not_3_out);
  or or_1 (not_2_out[3], and_1_out, and_2_out, and_3_out);
  not not_5 (not_5_out[2], in_2[2]);
  // NOT_Gate not_6 has open pins: in=in_2[3], out=open
  Hex_Digit_Display hex_digit_display_2 (.value({not_5_out, in_2[1:0]}));  // open: dp
  // NOT_Gate not_7 has open pins: in=in_2[1], out=open
  // NOT_Gate not_8 has open pins: in=in_2[0], out=open
  xor xor_2 (not_5_out[3], in_2[3], in_2[2]);
  not not_9 (not_9_out, in_3[3]);
  not not_10 (not_10_out, in_3[2]);
  not not_11 (not_11_out, in_3[1]);
  Hex_Digit_Display hex_digit_display_3 (.value(not_12_out));  // open: dp
  not not_12 (not_12_out[0], in_3[0]);
  and and_4 (and_4_out, not_10_out, not_11_out);
  and and_5 (and_5_out, in_3[2], in_3[1], in_3[0]);
  and and_6 (and_6_out, not_10_out, not_12_out[0]);
  and and_7 (and_7_out, not_9_out, in_3[2]);
  and and_8 (and_8_out, not_9_out, in_3[1], in_3[0]);
  and and_9 (and_9_out, in_3[3], in_3[2], not_12_out[0]);
  and and_10 (and_10_out, in_3[3], not_10_out, not_11_out);
  xor xor_3 (not_12_out[1], in_3[1], in_3[0]);
  or or_2 (not_12_out[2], and_4_out, and_5_out, and_6_out);
  or or_3 (not_12_out[3], and_7_out, and_8_out, and_9_out, and_10_out);
  not not_13 (not_13_out, in_4[3]);
  not not_14 (not_14_out, in_4[2]);
  not not_15 (not_15_out[1], in_4[1]);
  Hex_Digit_Display hex_digit_display_4 (.value({not_15_out, in_4[0]}));  // open: dp
  // NOT_Gate not_16 has open pins: in=in_4[0], out=open
  xor xor_4 (not_15_out[2], in_4[2], in_4[1]);
  and and_11 (and_11_out, in_4[3], not_15_out[1]);
  and and_12 (and_12_out, not_13_out, in_4[2], in_4[1]);
  and and_13 (and_13_out, in_4[3], not_14_out);
  or or_4 (not_15_out[3], and_11_out, and_12_out, and_13_out);
endmodule
