// Logisim project prueba codificacion 2.circ as structural Verilog: 1 circuit, main circuit main
module main (
  input  [3:0] in_1,
  input  [3:0] in_2
);

  wire and_1_out, and_2_out, and_3_out, and_4_out, and_5_out, not_1_out, not_2_out, not_3_out, not_4_out,
       not_5_out;
  wire [3:0] adder_1_out;
  wire [3:1] not_6_out;

  Hex_Digit_Display hex_digit_display_1 (.value(in_2));  // open: dp
  not not_1 (not_1_out, in_2[1]);
  not not_2 (not_2_out, in_2[3]);
  and and_1 (and_1_out, not_2_out, in_2[2], in_2[1]);
  and and_2 (and_2_out, in_2[3], not_1_out);
  or or_1 (not_6_out[3], and_2_out, and_1_out, and_3_out);
  and and_3 (and_3_out, in_2[3], not_4_out);
  Adder #(.width(4)) adder_1 (.a(in_1), .b(in_2), .out(adder_1_out));  // open: cin, cout
  not not_3 (not_3_out, in_2[1]);
  not not_4 (not_4_out, in_2[2]);
  and and_4 (and_4_out, in_2[2], not_3_out);
  Hex_Digit_Display hex_digit_display_2 (.value(adder_1_out));  // open: dp
  not not_5 (not_5_out, in_2[2]);
  and and_5 (and_5_out, in_2[1], not_5_out);
  or or_2 (not_6_out[2], and_4_out, and_5_out);
  not not_6 (not_6_out[1], in_2[1]);
  Hex_Digit_Display hex_digit_display_3 (.value({not_6_out, in_2[0]}));  // open: dp
endmodule
