// Logisim project prueba codificacion 4.circ as structural Verilog: 1 circuit, main circuit main
module main (
  input  [3:0] in_1,
  input  [3:0] in_2
);

  wire [3:0] adder_1_out;
  wire [3:2] not_1_out;

  xor xor_1 (not_1_out[3], in_1[3], in_1[2]);
  not not_1 (not_1_out[2], in_1[2]);
  Hex_Digit_Display hex_digit_display_1 (.value(adder_1_out));  // open: dp
  Adder #(.width(4)) adder_1 (.a(in_1), .b(in_2), .out(adder_1_out));  // open: cin, cout
  Hex_Digit_Display hex_digit_display_2 (.value({not_1_out, in_1[1:0]}));  // open: dp
endmodule
