// Logisim project prueba codificacion 5.circ as structural Verilog: 1 circuit, main circuit main
module main (
  input  [3:0] in_1,
  input  [3:0] in_2
);

  wire and_1_out, and_2_out, and_3_out, and_4_out, and_5_out, and_6_out, and_7_out, not_1_out, not_2_out,
       not_3_out;
  wire [3:0] adder_1_out, not_4_out;

  and and_1 (and_1_out, in_2[3], not_2_out, not_4_out[0]);
  not not_1 (not_1_out, in_2[3]);
  and and_2 (and_2_out, not_1_out, in_2[2]);
  and and_3 (and_3_out, not_1_out, in_2[1], in_2[0]);
  or or_1 (not_4_out[3], and_1_out, and_2_out, and_3_out, and_5_out);
  and and_4 (and_4_out, in_2[2], in_2[1], in_2[0]);
  and and_5 (and_5_out, in_2[3], not_2_out, not_3_out);
  not not_2 (not_2_out, in_2[2]);
  and and_6 (and_6_out, not_2_out, not_4_out[0]);
  Adder #(.width(4)) adder_1 (.a(in_2), .b(in_1), .out(adder_1_out));  // open: cin, cout
  not not_3 (not_3_out, in_2[1]);
  and and_7 (and_7_out, not_2_out, not_3_out);
  or or_2 (not_4_out[2], and_4_out, and_6_out, and_7_out);
  not not_4 (not_4_out[0], in_2[0]);
  xor xor_1 (not_4_out[1], in_2[1], in_2[0]);
  Hex_Digit_Display hex_digit_display_1 (.value(adder_1_out));  // open: dp
  Hex_Digit_Display hex_digit_display_2 (.value(not_4_out));  // open: dp
endmodule
